// Logisim project alu.circ as structural Verilog: 9 circuits, main circuit alu
module alu (
  input  [31:0] A,
  input  [31:0] B,
  input  [3:0] ALUSel,
  output [31:0] Result
);

  wire [31:0] add0, and0, bsel0, mul0, mulh0, mulhu0, mux4_1, mux4_2, mux4_3, mux4_4, or0, sll1, slt1, sra1,
       srl1, sub0, xor0;

  Adder #(.width(32)) adder_1 (.a(A), .b(B), .out(add0));  // open: cin, cout
  assign and0 = A & B;  // AND_Gate and_1, 32 bits wide
  assign or0 = A | B;  // OR_Gate or_1, 32 bits wide
  assign xor0 = A ^ B;  // XOR_Gate xor_1, 32 bits wide
  Multiplier #(.mode("twosComplement"), .width(32)) multiplier_1 (.a(A), .b(B), .out(mul0));  // open: cin, cout
  Subtractor #(.width(32)) subtractor_1 (.a(A), .b(B), .out(sub0));  // open: bin, bout
  srl0 srl0_1 (.in_1(A), .in_2(B), .out_3(srl1));
  sra0 sra0_1 (.in_1(A), .in_2(B), .out_3(sra1));
  sll0 sll0_1 (.in_1(A), .in_2(B), .out_3(sll1));
  slt slt_1 (.in_1(A), .in_2(B), .out_3(slt1));
  MULHU mulhu_1 (.in_1(A), .in_2(B), .out_3(mulhu0));
  bsel bsel_1 (.in_1(A), .in_2(B), .out_3(bsel0));
  MULH mulh_1 (.in_1(A), .in_2(B), .out_3(mulh0));
  mux4 u_mux4_1 (
    .in_1(mux4_1), .in_2(mux4_2), .in_3(mux4_3), .in_4(mux4_4), .in_5(ALUSel[2]), .in_6(ALUSel[3]),
    .out_7(Result));
  mux4 u_mux4_2 (.in_1(add0), .in_2(and0), .in_3(or0), .in_4(xor0), .in_5(ALUSel[0]), .in_6(ALUSel[1]), .out_7(mux4_1));
  mux4 u_mux4_3 (
    .in_1(srl1), .in_2(sra1), .in_3(sll1), .in_4(slt1), .in_5(ALUSel[0]), .in_6(ALUSel[1]), .out_7(mux4_2));
  mux4 u_mux4_4 (.in_3(mul0), .in_4(mulhu0), .in_5(ALUSel[0]), .in_6(ALUSel[1]), .out_7(mux4_3));  // open: in_1, in_2
  mux4 mux4_5 (
    .in_1(sub0), .in_2(bsel0), .in_3(mulh0), .in_5(ALUSel[0]), .in_6(ALUSel[1]), .out_7(mux4_4));  // open: in_4

  // Notes on the sheet:
  //   INPUTS to your circuit
  //   DON'T CHANGE THE LOCATIONS OF THE INPUTS AND OUTPUTS!
  //   OUTPUT from your circuit
endmodule

module MULH (
  input  [31:0] in_1,
  input  [31:0] in_2,
  output [31:0] out_3
);

  wire [31:0] multiplier_1_out;
  wire [63:0] bit_extender_1_out, bit_extender_2_out;

  assign bit_extender_1_out = {{32{in_1[31]}}, in_1};  // Bit_Extender bit_extender_1
  assign bit_extender_2_out = {{32{in_2[31]}}, in_2};  // Bit_Extender bit_extender_2
  Multiplier #(.mode("twosComplement"), .width(64)) multiplier_1 (
    .a(bit_extender_1_out), .b(bit_extender_2_out), .out({out_3, multiplier_1_out}));  // open: cin, cout
endmodule

module MULHU (
  input  [31:0] in_1,
  input  [31:0] in_2,
  output [31:0] out_3
);

  wire [31:0] multiplier_1_out;
  wire [63:0] bit_extender_1_out, bit_extender_2_out;

  assign bit_extender_1_out = {{32{1'b0}}, in_1};  // Bit_Extender bit_extender_1
  assign bit_extender_2_out = {{32{1'b0}}, in_2};  // Bit_Extender bit_extender_2
  Multiplier #(.width(64)) multiplier_1 (
    .a(bit_extender_1_out), .b(bit_extender_2_out), .out({out_3, multiplier_1_out}));  // open: cin, cout
endmodule

module slt (
  input  [31:0] in_1,
  input  [31:0] in_2,
  output [31:0] out_3
);

  wire comparator_1_lt;

  Comparator #(.width(32)) comparator_1 (.a(in_1), .b(in_2), .lt(comparator_1_lt));  // open: gt, eq
  Multiplexer #(.enable("false"), .width(32)) multiplexer_1 (
    .in0({32{1'b0}}), .in1(32'h1), .out(out_3), .sel(comparator_1_lt));
endmodule

module srl0 (
  input  [31:0] in_1,
  input  [31:0] in_2,
  output [31:0] out_3
);

  Shifter #(.shift("lr"), .width(32)) shifter_1 (.in(in_1), .\dist (in_2[4:0]), .out(out_3));
endmodule

module sra0 (
  input  [31:0] in_1,
  input  [31:0] in_2,
  output [31:0] out_3
);

  Shifter #(.shift("ar"), .width(32)) shifter_1 (.in(in_1), .\dist (in_2[4:0]), .out(out_3));
endmodule

module sll0 (
  input  [31:0] in_1,
  input  [31:0] in_2,
  output [31:0] out_3
);

  Shifter #(.width(32)) shifter_1 (.in(in_1), .\dist (in_2[4:0]), .out(out_3));
endmodule

module bsel (
  input  [31:0] in_1,
  input  [31:0] in_2,
  output [31:0] out_3
);

  Multiplexer #(.enable("false"), .width(32)) multiplexer_1 (.in0(in_1), .in1(in_2), .out(out_3), .sel(1'b1));
endmodule

module mux4 (
  input  [31:0] in_1,
  input  [31:0] in_2,
  input  [31:0] in_3,
  input  [31:0] in_4,
  input  in_5,
  input  in_6,
  output [31:0] out_7
);

  wire [31:0] multiplexer_1_out, multiplexer_2_out;

  Multiplexer #(.enable("false"), .width(32)) multiplexer_1 (
    .in0(in_1), .in1(in_2), .out(multiplexer_1_out), .sel(in_5));
  Multiplexer #(.enable("false"), .width(32)) multiplexer_2 (
    .in0(in_3), .in1(in_4), .out(multiplexer_2_out), .sel(in_5));
  Multiplexer #(.enable("false"), .width(32)) multiplexer_3 (
    .in0(multiplexer_1_out), .in1(multiplexer_2_out), .out(out_7), .sel(in_6));
endmodule
