// Logisim project control_logic.circ as structural Verilog: 1 circuit, main circuit control_logic
module control_logic (
  input  [31:0] inst,
  input  BrEq,
  input  BrLt,
  output PCSel,
  output RegWEn,
  output [2:0] ImmSel,
  output BrUn,
  output ASel,
  output BSel,
  output [3:0] ALUSel,
  output MemRW,
  output [1:0] WBSel,
  output CSRSel,
  output CSRWen
);

  wire and0_out, and_2_out, and_3_out, and_4_out, and_5_out, and_6_out, and_7_out, and_8_out, and_9_out,
       auipc_out, B_out, Beq_out, Bge_out, Bgeu_out, Blt_out, Bltu_out, Bne_out, funct3001_out,
       funct3101_out, I_out, Ifunct3101_out, Itype0_out, Itype_out, jal_out, jalr_out, LOAD_out, lui_out,
       mul1_out, mul3_out, mulh1_out, mulh3_out, mulhu0_out, mulhu1_out, mulhu3_out, not_1_out, not_2_out,
       not_3_out, not_4_out, not_5_out, not_6_out, not_7_out, not_8_out, not_9_out, not_10_out, not_11_out,
       not_12_out, not_13_out, not_14_out, not_15_out, not_16_out, not_17_out, not_18_out, not_19_out,
       not_20_out, not_21_out, not_22_out, not_23_out, not_24_out, not_25_out, not_26_out, not_27_out,
       not_28_out, not_29_out, not_30_out, not_31_out, not_32_out, not_33_out, not_34_out, not_35_out,
       not_36_out, not_37_out, not_38_out, not_39_out, not_40_out, not_41_out, not_42_out, not_43_out,
       not_44_out, not_45_out, not_46_out, not_47_out, not_48_out, not_49_out, not_50_out, not_51_out,
       not_52_out, not_53_out, not_54_out, not_55_out, not_56_out, not_57_out, not_58_out, not_59_out,
       not_60_out, not_61_out, not_62_out, not_63_out, not_64_out, not_65_out, not_66_out, not_67_out,
       not_68_out, not_69_out, not_70_out, not_71_out, not_72_out, not_73_out, not_74_out, not_75_out,
       not_76_out, not_77_out, not_78_out, not_79_out, not_80_out, not_81_out, not_82_out, or1_out, or_1_out,
       or_2_out, or_3_out, or_4_out, R_out, Rtype0_out, Rtype_out, sll1_out, slli_out, slt0_out, slt1_out,
       slt2_out, slti_out, sra0_out, sub2_out, sub3_out, xor0_out, xor1_out;

  and Bgeu (Bgeu_out, inst[14], inst[13], inst[12], not_7_out);
  not not_1 (not_1_out, inst[14]);
  and mulhu3 (mulhu3_out, inst[25], not_1_out, inst[13], inst[12]);
  not not_2 (not_2_out, inst[13]);
  not not_3 (not_3_out, inst[14]);
  and Ifunct3101 (Ifunct3101_out, inst[14], not_2_out, inst[12]);
  not not_4 (not_4_out, inst[12]);
  and or1 (or1_out, inst[14], inst[13], not_4_out);
  not not_5 (not_5_out, inst[14]);
  not not_6 (not_6_out, inst[12]);
  and slt0 (slt0_out, not_5_out, inst[13], not_6_out);
  not not_7 (not_7_out, BrLt);
  not not_8 (not_8_out, inst[12]);
  and Bltu (Bltu_out, inst[14], inst[13], not_8_out, BrLt);
  not not_9 (not_9_out, inst[14]);
  not not_10 (not_10_out, inst[13]);
  and mulh3 (mulh3_out, inst[25], not_9_out, not_10_out, inst[12]);
  not not_11 (not_11_out, inst[12]);
  not not_12 (not_12_out, inst[14]);
  and slti (slti_out, not_3_out, inst[13], not_11_out);
  not not_13 (not_13_out, inst[13]);
  not not_14 (not_14_out, inst[12]);
  and xor1 (xor1_out, inst[14], not_13_out, not_14_out);
  not not_15 (not_15_out, inst[13]);
  not not_16 (not_16_out, inst[12]);
  and xor0 (xor0_out, inst[14], not_15_out, not_16_out);
  not not_17 (not_17_out, inst[13]);
  not not_18 (not_18_out, BrLt);
  and Bge (Bge_out, inst[14], not_17_out, inst[12], not_18_out);
  not not_19 (not_19_out, inst[14]);
  not not_20 (not_20_out, inst[12]);
  not not_21 (not_21_out, inst[14]);
  not not_22 (not_22_out, inst[13]);
  and sub3 (sub3_out, inst[30], not_19_out, not_22_out, not_20_out);
  not not_23 (not_23_out, inst[13]);
  not not_24 (not_24_out, inst[13]);
  and slli (slli_out, not_12_out, not_23_out, inst[12]);
  and funct3101 (funct3101_out, inst[14], not_24_out, inst[12]);
  not not_25 (not_25_out, inst[14]);
  not not_26 (not_26_out, inst[12]);
  not not_27 (not_27_out, inst[14]);
  and slt1 (slt1_out, not_25_out, inst[13], not_26_out);
  not not_28 (not_28_out, inst[13]);
  and sra0 (sra0_out, inst[30], inst[14], not_28_out, inst[12]);
  not not_29 (not_29_out, inst[13]);
  not not_30 (not_30_out, inst[12]);
  and Blt (Blt_out, inst[14], not_29_out, not_30_out, BrLt);
  not not_31 (not_31_out, inst[12]);
  not not_32 (not_32_out, inst[13]);
  and mul3 (mul3_out, inst[25], not_21_out, not_32_out, not_31_out);
  not not_33 (not_33_out, inst[14]);
  and slt2 (slt2_out, not_33_out, inst[13], not_41_out);
  not not_34 (not_34_out, inst[13]);
  not not_35 (not_35_out, inst[14]);
  and sll1 (sll1_out, not_27_out, not_34_out, inst[12]);
  not not_36 (not_36_out, inst[14]);
  and and0 (and0_out, inst[14], inst[13], inst[12]);
  and mulhu0 (mulhu0_out, not_36_out, inst[13], inst[12]);
  not not_37 (not_37_out, inst[13]);
  not not_38 (not_38_out, BrEq);
  not not_39 (not_39_out, inst[14]);
  not not_40 (not_40_out, inst[14]);
  and Bne (Bne_out, not_39_out, not_37_out, inst[12], not_38_out);
  or or_1 (or_1_out, mul3_out, sub3_out, mulh3_out, mulhu3_out);
  not not_41 (not_41_out, inst[12]);
  not not_42 (not_42_out, inst[14]);
  not not_43 (not_43_out, inst[13]);
  and funct3001 (funct3001_out, not_42_out, not_43_out, inst[12]);
  not not_44 (not_44_out, inst[14]);
  and mulhu1 (mulhu1_out, not_35_out, inst[13], inst[12]);
  and mulh1 (mulh1_out, inst[25], not_44_out, not_50_out, inst[12]);
  not not_45 (not_45_out, inst[13]);
  not not_46 (not_46_out, inst[12]);
  and Beq (Beq_out, not_40_out, not_45_out, not_46_out, BrEq);
  not not_47 (not_47_out, inst[14]);
  not not_48 (not_48_out, inst[12]);
  not not_49 (not_49_out, inst[13]);
  and sub2 (sub2_out, inst[30], not_47_out, not_49_out, not_48_out);
  not not_50 (not_50_out, inst[13]);
  not not_51 (not_51_out, inst[14]);
  not not_52 (not_52_out, inst[13]);
  and mul1 (mul1_out, inst[25], not_51_out, not_52_out, not_53_out);
  or or_2 (or_2_out, Beq_out, Bne_out, Blt_out, Bge_out, Bltu_out, Bgeu_out);
  or or_3 (or_3_out, sub2_out, funct3001_out, slt2_out, funct3101_out);
  or or_4 (or_4_out, slli_out, slti_out, Ifunct3101_out);
  not not_53 (not_53_out, inst[12]);
  or Rtype (Rtype_out, mul1_out, mulh1_out, mulhu1_out, sll1_out, slt1_out, xor1_out, or1_out);
  or Itype (Itype_out, sll1_out, slt1_out, xor1_out, or1_out);
  or Rtype0 (Rtype0_out, mulhu0_out, and0_out, sra0_out, xor0_out, slt0_out);
  or Itype0 (Itype0_out, and0_out, sra0_out, xor0_out, slt0_out);
  and csrw (CSRWen, inst[6], inst[5], inst[4], not_55_out, not_54_out, inst[1], inst[0]);
  not not_54 (not_54_out, inst[2]);
  not not_55 (not_55_out, inst[3]);
  not not_56 (not_56_out, inst[4]);
  not not_57 (not_57_out, inst[4]);
  not not_58 (not_58_out, inst[3]);
  and jalr (jalr_out, inst[6], inst[5], not_56_out, not_58_out, inst[2], inst[1], inst[0]);
  not not_59 (not_59_out, inst[6]);
  and jal (jal_out, inst[6], inst[5], not_57_out, inst[3], inst[2], inst[1], inst[0]);
  not not_60 (not_60_out, inst[3]);
  not not_61 (not_61_out, inst[5]);
  not not_62 (not_62_out, inst[6]);
  and lui (lui_out, not_59_out, inst[5], inst[4], not_60_out, inst[2], inst[1], inst[0]);
  and and_1 (CSRSel, inst[14], CSRWen);
  not not_63 (not_63_out, inst[3]);
  not not_64 (not_64_out, inst[4]);
  and auipc (auipc_out, not_62_out, not_61_out, inst[4], not_63_out, inst[2], inst[1], inst[0]);
  not not_65 (not_65_out, inst[2]);
  not not_66 (not_66_out, inst[6]);
  not not_67 (not_67_out, inst[4]);
  not not_68 (not_68_out, inst[3]);
  and B (B_out, inst[6], inst[5], not_64_out, not_68_out, not_65_out, inst[1], inst[0]);
  not not_69 (not_69_out, inst[2]);
  not not_70 (not_70_out, inst[5]);
  not not_71 (not_71_out, inst[3]);
  not not_72 (not_72_out, inst[6]);
  and SAVE (MemRW, not_66_out, inst[5], not_67_out, not_71_out, not_69_out, inst[1], inst[0]);
  not not_73 (not_73_out, inst[2]);
  not not_74 (not_74_out, inst[6]);
  not not_75 (not_75_out, inst[4]);
  not not_76 (not_76_out, inst[3]);
  not not_77 (not_77_out, inst[5]);
  and I (I_out, not_72_out, not_70_out, inst[4], not_76_out, not_73_out, inst[1], inst[0]);
  and and_2 (and_2_out, B_out, or_2_out);
  not not_78 (not_78_out, inst[2]);
  not not_79 (not_79_out, inst[6]);
  not not_80 (not_80_out, inst[3]);
  and LOAD (LOAD_out, not_74_out, not_77_out, not_75_out, not_80_out, not_78_out, inst[1], inst[0]);
  not not_81 (not_81_out, inst[2]);
  not not_82 (not_82_out, inst[3]);
  and R (R_out, not_79_out, inst[5], inst[4], not_82_out, not_81_out, inst[1], inst[0]);
  and and_3 (and_3_out, R_out, or_1_out);
  and and_4 (and_4_out, R_out, or_3_out);
  and and_5 (and_5_out, I_out, or_4_out);
  and and_6 (and_6_out, R_out, Rtype_out);
  and and_7 (and_7_out, I_out, Itype_out);
  and and_8 (and_8_out, R_out, Rtype0_out);
  and and_9 (and_9_out, I_out, Itype0_out);
  or ASel0 (ASel, B_out, auipc_out, jal_out);
  or BSel0 (BSel, LOAD_out, I_out, MemRW, B_out, auipc_out, lui_out, jal_out, jalr_out);
  or RWEn0 (RegWEn, R_out, LOAD_out, I_out, auipc_out, lui_out, jal_out, jalr_out);
  or WB1 (WBSel[1], jal_out, jalr_out);
  or WB0 (WBSel[0], R_out, I_out, auipc_out, lui_out);
  or imm0 (ImmSel[0], MemRW, auipc_out, lui_out);
  or imm1 (ImmSel[1], B_out, auipc_out, lui_out);
  buf imm2 (ImmSel[2], jal_out);  // OR_Gate
  and BrUn0 (BrUn, inst[13], inst[14], B_out);
  or PcSel0 (PCSel, and_2_out, jal_out, jalr_out);
  or ALUop3 (ALUSel[3], and_3_out, lui_out);
  or ALUop2 (ALUSel[2], lui_out, and_4_out, and_5_out);
  or ALUop1 (ALUSel[1], and_6_out, and_7_out);
  or ALUop0 (ALUSel[0], and_8_out, lui_out, and_9_out);

  // Other names for the same wires on the sheet: funct3[2:0] = inst[14:12]; funct7[6:0] = inst[31:25]

  // Notes on the sheet:
  //   INPUTS to your circuit
  //   DON'T CHANGE THE LOCATIONS OF THE INPUTS AND OUTPUTS!
  //   OUTPUT from your circuit
endmodule
