// Logisim project cpu.circ as structural Verilog: 1 circuit, main circuit cpu
module cpu (
  input  clk,
  input  [31:0] INSTRUCTION,
  input  [31:0] READ_DATA,
  output [31:0] WRITE_ADDRESS,
  output [31:0] PROGRAM_COUNTER,
  output [31:0] ra,
  output [31:0] sp,
  output [31:0] t0,
  output [31:0] t1,
  output [31:0] t2,
  output [31:0] s0,
  output [31:0] s1,
  output [31:0] a0,
  output [31:0] tohost,
  output [3:0] WRITE_ENABLE,
  output [31:0] WRITE_DATA
);

  wire branch_comp_1_breq, branch_comp_1_brlt, control_logic_1_asel, control_logic_1_brun,
       control_logic_1_bsel, control_logic_1_csrsel, control_logic_1_csrwen, control_logic_1_memrw,
       control_logic_1_pcsel, control_logic_1_regwen, not_1_out, register_3_q;
  wire [1:0] control_logic_1_wbsel;
  wire [2:0] control_logic_1_immsel, funct3, multiplexer_2_out_3;
  wire [3:0] control_logic_1_alusel;
  wire [4:0] multiplexer_2_out_2, multiplexer_2_out_4, multiplexer_3_out, multiplexer_4_out,
       multiplexer_5_out;
  wire [6:0] multiplexer_2_out;
  wire [11:0] multiplexer_2_out_5;
  wire [15:0] regfile_1_read_data_2, regfile_1_read_data_2_2;
  wire [31:0] adder_1_out, adder_2_out, bit_extender_1_out, bit_extender_2_out, bit_extender_3_out,
       imm_gen_1_imm, multiplexer_1_out, multiplexer_6_out, multiplexer_8_out, multiplexer_9_out,
       multiplexer_10_out, multiplexer_12_out, regfile_1_read_data_1, register_1_q, register_2_q;

  Adder #(.width(32)) adder_1 (.a(PROGRAM_COUNTER), .b(32'h4), .out(adder_1_out));  // open: cin, cout
  Register #(.width(32)) PC (.D(multiplexer_1_out), .en(1'b1), .clk(clk), .Q(PROGRAM_COUNTER));  // open: clr
  Multiplexer #(.enable("false"), .width(32)) multiplexer_1 (
    .in0(adder_1_out), .in1(WRITE_ADDRESS), .out(multiplexer_1_out), .sel(control_logic_1_pcsel));
  Register #(.width(32)) register_1 (
    .D(INSTRUCTION), .en(1'b1), .clk(clk), .Q({register_1_q[31:15], funct3, register_1_q[11:0]}));  // open: clr
  Register #(.width(32)) register_2 (.D(PROGRAM_COUNTER), .en(1'b1), .clk(clk), .Q(register_2_q));  // open: clr
  not not_1 (not_1_out, control_logic_1_pcsel);
  Register #(.width(1)) register_3 (.D(not_1_out), .en(1'b1), .clk(clk), .Q(register_3_q));  // open: clr
  Multiplexer #(.enable("false"), .width(32)) multiplexer_2 (
    .in0(32'h13), .in1({register_1_q[31:15], funct3, register_1_q[11:0]}),
    .out({multiplexer_2_out_5, multiplexer_2_out_4, multiplexer_2_out_3, multiplexer_2_out_2, multiplexer_2_out}),
    .sel(register_3_q));
  control_logic control_logic_1 (
    .CSRWen(control_logic_1_csrwen), .PCSel(control_logic_1_pcsel), .RegWEn(control_logic_1_regwen),
    .ImmSel(control_logic_1_immsel), .BrUn(control_logic_1_brun), .ASel(control_logic_1_asel),
    .BSel(control_logic_1_bsel), .ALUSel(control_logic_1_alusel), .MemRW(control_logic_1_memrw),
    .WBSel(control_logic_1_wbsel), .CSRSel(control_logic_1_csrsel),
    .inst({multiplexer_2_out_5, multiplexer_2_out_4, multiplexer_2_out_3, multiplexer_2_out_2, multiplexer_2_out}),
    .BrEq(branch_comp_1_breq), .BrLt(branch_comp_1_brlt));
  Multiplexer #(.enable("false"), .width(5)) multiplexer_3 (
    .in0({5{1'b0}}), .in1(register_1_q[19:15]), .out(multiplexer_3_out), .sel(register_3_q));
  Multiplexer #(.enable("false"), .width(5)) multiplexer_4 (
    .in0({5{1'b0}}), .in1(register_1_q[24:20]), .out(multiplexer_4_out), .sel(register_3_q));
  Multiplexer #(.enable("false"), .width(5)) multiplexer_5 (
    .in0({5{1'b0}}), .in1(register_1_q[11:7]), .out(multiplexer_5_out), .sel(register_3_q));
  Multiplexer #(.enable("false"), .width(32)) multiplexer_6 (
    .in0(32'h13), .in1({register_1_q[31:15], funct3, register_1_q[11:0]}), .out(multiplexer_6_out),
    .sel(register_3_q));
  imm_gen imm_gen_1 (.inst(multiplexer_6_out), .ImmSel(control_logic_1_immsel), .imm(imm_gen_1_imm));
  Multiplexer #(.enable("false"), .width(4)) multiplexer_7 (
    .in0(4'b0000), .in1(4'b1111), .out(WRITE_ENABLE), .sel(control_logic_1_memrw));
  regfile regfile_1 (
    .rs1(multiplexer_3_out), .rs2(multiplexer_4_out), .rd(multiplexer_5_out),
    .Write_Data(multiplexer_12_out), .RegWEn(control_logic_1_regwen), .clk(clk), .ra(ra), .sp(sp), .t0(t0),
    .t1(t1), .t2(t2), .s0(s0), .s1(s1), .a0(a0), .Read_Data_1(regfile_1_read_data_1),
    .Read_Data_2({regfile_1_read_data_2_2, regfile_1_read_data_2}));
  assign bit_extender_1_out = {{27{1'b0}}, multiplexer_2_out_4};  // Bit_Extender bit_extender_1
  Multiplexer #(.enable("false"), .width(32)) multiplexer_8 (
    .in0(regfile_1_read_data_1), .in1(bit_extender_1_out), .out(multiplexer_8_out),
    .sel(control_logic_1_csrsel));
  branch_comp branch_comp_1 (
    .rs1(regfile_1_read_data_1), .rs2({regfile_1_read_data_2_2, regfile_1_read_data_2}),
    .BrUn(control_logic_1_brun), .BrEq(branch_comp_1_breq), .BrLt(branch_comp_1_brlt));
  csr csr_1 (
    .CSR_address(multiplexer_2_out_5), .CSR_din(multiplexer_8_out), .CSR_WE(control_logic_1_csrwen),
    .clk(clk), .tohost(tohost));
  Multiplexer #(.enable("false"), .width(32)) multiplexer_9 (
    .in0(regfile_1_read_data_1), .in1(register_2_q), .out(multiplexer_9_out), .sel(control_logic_1_asel));
  Multiplexer #(.enable("false"), .width(32)) multiplexer_10 (
    .in0({regfile_1_read_data_2_2, regfile_1_read_data_2}), .in1(imm_gen_1_imm), .out(multiplexer_10_out),
    .sel(control_logic_1_bsel));
  alu alu_1 (.Result(WRITE_ADDRESS), .A(multiplexer_9_out), .B(multiplexer_10_out), .ALUSel(control_logic_1_alusel));
  assign bit_extender_2_out = {{24{regfile_1_read_data_2[7]}}, regfile_1_read_data_2[7:0]};  // Bit_Extender bit_extender_2
  assign bit_extender_3_out = {{16{regfile_1_read_data_2[15]}}, regfile_1_read_data_2};  // Bit_Extender bit_extender_3
  Adder #(.width(32)) adder_2 (.a(register_2_q), .b(32'h4), .out(adder_2_out));  // open: cin, cout
  Multiplexer #(.enable("false"), .select(2), .width(32)) multiplexer_11 (
    .in0(bit_extender_2_out), .in1(bit_extender_3_out),
    .in2({regfile_1_read_data_2_2, regfile_1_read_data_2}), .out(WRITE_DATA), .sel(funct3[1:0]));  // open: in3
  Multiplexer #(.enable("false"), .select(2), .width(32)) multiplexer_12 (
    .in0(READ_DATA), .in1(WRITE_ADDRESS), .in2(adder_2_out), .out(multiplexer_12_out),
    .sel(control_logic_1_wbsel));  // open: in3

  // Notes on the sheet:
  //   Output to IMEM
  //   IMEM (do **NOT** move this)
  //   Inputs from IMEM
  //   It is OK to move the PC, RegFile, ALU, MEM, Branch Comp, Imm Gen, and Control Logic to wherever is most convenient for you when constructing your CPU, and to delete this text
  //   Inputs/Outputs for testing. Do **NOT** move these.
  //   Outputs To DMEM
  //   DMEM (do **NOT** move this)
  //   Inputs From DMEM
endmodule
